// Logisim project CPU-latest.circ as structural Verilog: 5 circuits, main circuit main
module main (
  input  Reset,
  input  Single_Step_Mode
);

  wire ALU_EN, and_2_out, and_3_out, and_4_out, CLK, clock_1_out, cu_1_dbg_cmd, cu_1_flag_wr_en, cu_1_ici,
       cu_1_incpc, cu_1_mov_r2r, cu_1_reg_wr_en, decoder_1_out0, decoder_1_out1, decoder_1_out2,
       decoder_1_out3, decoder_1_out4, decoder_1_out5, decoder_1_out6, decoder_1_out7, LDC_EN, LDs12C_ALU,
       Mem_EN, Mem_WR_EN, MOV_R2PC, not_1_out, not_2_out, or_1_out, or_2_out, PC2ALU_A, Reg_A_EN,
       Release_DBG_out, s_r_ff_1_qn;
  wire [2:0] cu_1_a, cu_1_b, cu_1_c, cu_1_result;
  wire [3:0] FlagsIn, FlagsOut;
  wire [4:0] cu_1_alu_cmd;
  wire [7:0] keyboard_1_data;
  wire [9:0] undriven;
  wire [14:0] cpu_register_1_portb;
  wire [15:0] alu_1_res, bit_extender_1_out, controlled_buffer_2_out, controlled_buffer_5_out,
       cpu_register_1_porta, cpu_register_1_portc, cu_1_ldc, PC_q, random_1_out, Result;
  wire [15:15] cpu_register_1_portb_2;
  wire [19:0] MEM_BUS_OUT;

  Clock clock_1 (.out(clock_1_out));
  Button Release_DBG (.out(Release_DBG_out));
  S_R_Flip_Flop s_r_ff_1 (
    .S(or_1_out), .R(1'b0), .clk(clock_1_out), .reset(Release_DBG_out), .Qn(s_r_ff_1_qn));  // open: Q, preset
  or or_1 (or_1_out, cu_1_dbg_cmd, Single_Step_Mode);
  CU cu_1 (
    .PMemBus(MEM_BUS_OUT), .CLK(CLK), .Reset(Reset), .Flags(FlagsIn), .IncPC(cu_1_incpc),
    .ALU_CMD(cu_1_alu_cmd), .A(cu_1_a), .B(cu_1_b), .C(cu_1_c), .Result(cu_1_result),
    .Reg_WR_EN(cu_1_reg_wr_en), .LDC_EN(LDC_EN), .ALU_EN(ALU_EN), .MOV_R2R(cu_1_mov_r2r),
    .MOV_R2PC(MOV_R2PC), .LDs12C_ALU(LDs12C_ALU), .Reg_A_EN(Reg_A_EN), .PC2ALU_A(PC2ALU_A),
    .Flag_WR_EN(cu_1_flag_wr_en), .Mem_EN(Mem_EN), .Mem_WR_EN(Mem_WR_EN), .LDC(cu_1_ldc), .ICI(cu_1_ici),
    .DBG_cmd(cu_1_dbg_cmd));  // open: out_6, out_7, out_8, out_25
  Counter #(.max('hffff), .width(16)) PC (
    .load(MOV_R2PC), .D(Result), .count(cu_1_incpc), .Q(PC_q), .clk(CLK), .clr(Reset));  // open: carry, up
  assign Result = LDC_EN ? cu_1_ldc : 16'bz;  // Controlled_Buffer controlled_buffer_1
  not not_1 (not_1_out, cu_1_ici);
  LED ICNI (.in(not_1_out));
  and and_1 (CLK, cu_1_ici, clock_1_out, s_r_ff_1_qn);
  ROM #(.addrWidth(16), .dataWidth(20)) PRG_MEM (.addr(PC_q), .data(MEM_BUS_OUT));
  assign bit_extender_1_out = {{4{cu_1_ldc[15]}}, cu_1_ldc[15:4]};  // Bit_Extender bit_extender_1
  assign controlled_buffer_2_out = LDs12C_ALU ? bit_extender_1_out : 16'bz;  // Controlled_Buffer controlled_buffer_2
  assign Result = cu_1_mov_r2r ? controlled_buffer_5_out : 16'bz;  // Controlled_Buffer controlled_buffer_3
  Register #(.width(4)) register_1 (.D(FlagsOut), .en(cu_1_flag_wr_en), .clk(CLK), .Q(FlagsIn));  // open: clr
  assign Result = ALU_EN ? alu_1_res : 16'bz;  // Controlled_Buffer controlled_buffer_4
  assign controlled_buffer_5_out = Reg_A_EN ? cpu_register_1_porta : 16'bz;  // Controlled_Buffer controlled_buffer_5
  CPU_Register cpu_register_1 (
    .CLK(CLK), .AddrA(cu_1_a), .AddrB(cu_1_b), .AddrC(cu_1_c), .Reset(Reset), .PortIn(Result),
    .WR_EN(cu_1_reg_wr_en), .AddrIn(cu_1_result), .PortA(cpu_register_1_porta),
    .PortB({cpu_register_1_portb_2[15], cpu_register_1_portb}), .PortC(cpu_register_1_portc));
  assign controlled_buffer_5_out = PC2ALU_A ? PC_q : 16'bz;  // Controlled_Buffer controlled_buffer_6
  and and_2 (and_2_out, Mem_WR_EN, ~cpu_register_1_portb_2[15]);  // AND_Gate
  and and_3 (and_3_out, ~cpu_register_1_portb_2[15], Mem_EN);  // AND_Gate
  or or_2 (or_2_out, Mem_WR_EN, Mem_EN);
  not not_2 (not_2_out, LDs12C_ALU);
  RAM #(.addrWidth(15), .dataWidth(16), .databus("bidir"), .\type ("nonvolatile")) ram_1 (
    .addr(cpu_register_1_portb), .we(and_2_out), .oe(and_3_out), .clk(CLK), .data(Result));
  and and_4 (and_4_out, or_2_out, cpu_register_1_portb_2[15]);
  assign controlled_buffer_2_out = not_2_out ? {cpu_register_1_portb_2[15], cpu_register_1_portb} : 16'bz;  // Controlled_Buffer controlled_buffer_7
  ALU alu_1 (
    .A(controlled_buffer_5_out), .CMD(cu_1_alu_cmd), .B(controlled_buffer_2_out), .C(cpu_register_1_portc),
    .FlagsInp(FlagsIn), .Res(alu_1_res), .Flags(FlagsOut));
  Decoder #(.select(3)) decoder_1 (
    .out0(decoder_1_out0), .out1(decoder_1_out1), .out2(decoder_1_out2), .out3(decoder_1_out3),
    .out4(decoder_1_out4), .out5(decoder_1_out5), .out6(decoder_1_out6), .out7(decoder_1_out7),
    .sel(cpu_register_1_portb[2:0]), .en(and_4_out));
  TTY tty_1 (.data(Result[6:0]), .clk(decoder_1_out0), .we(decoder_1_out0), .clr(decoder_1_out1));
  Keyboard #(.trigger("falling")) keyboard_1 (
    .clk(decoder_1_out2), .re(1'b1), .clr(decoder_1_out3), .avail(keyboard_1_data[7]),
    .data(keyboard_1_data[6:0]));
  assign Result[9:0] = decoder_1_out4 ? undriven : 10'bz;  // Controlled_Buffer controlled_buffer_8
  Joystick #(.bits(5)) joystick_1 ();  // open: x, y
  Random #(.width(16)) random_1 (.clr(decoder_1_out5), .next(decoder_1_out6), .clk(CLK), .out(random_1_out));
  assign Result = decoder_1_out2 ? {{8{1'b0}}, keyboard_1_data} : 16'bz;  // Controlled_Buffer controlled_buffer_9
  assign Result = decoder_1_out7 ? random_1_out : 16'bz;  // Controlled_Buffer controlled_buffer_10

  // Notes on the sheet:
  //   contents of PRG_MEM (hex, n*v repeats v):
  //   2080 90 168 1080 792 168 5 69f 168 5 693 168 5 69b 168 5 799 168 80080 597 168 49f 168 592 168 494
  //   168 49c 168 495 168 290 168 29d 168 290 168 495 168 69e 168 794 168 695 168 792 168 290 168 799 168
  //   69f 168 795 168 792 168 290 168 697 168 795 168 695 168 793 168 168 39a 168 9a 168 80 20069 85 108
  //   1159 80082 a0069 90 d08 ff659 80080 568 58 93 80 40069 205 268 61100 1d68 d0 fea58 1080 20069 86 108
  //   4a59 80080 9a 168 1080 94 c0 f0 58 40069 60869 7df 62b09 5 105 405 1a08 559 58 5d8 800e0 3568 558
  //   2db 800e0 3568 705 58 d5 2f08 1759 2c08 fe85a 20d0 82869 405 2c68 58 80 68 84 90 a0 d5 58 268 105
  //   800 2908 ffb5a 80080 9a 168 fb058 80080 9a 168 80080 599 168 69f 168 795 168 290 168 797 168 699 168
  //   69e 168 291 168 7f 80080 9a 168 599 168 69f 168 795 168 290 168 69c 168 69f 168 793 168 695 168 291
  //   168 7f
endmodule

module ALU (
  input  [15:0] A,
  input  [15:0] B,
  input  [15:0] C,
  input  [3:0] FlagsInp,
  input  [4:0] CMD,
  output [15:0] Res,
  output [3:0] Flags
);

  wire adder_1_cout, adder_2_cout, adder_3_cout, adder_4_cout, adder_5_cout, subtractor_1_bout,
       subtractor_2_bout, subtractor_3_bout;
  wire [7:0] multiplier_1_cout, multiplier_1_out;
  wire [15:0] adder_1_out, adder_2_out, adder_3_out, adder_4_out, adder_5_out, and_1_out, negator_1_out,
       not_1_out, or_1_out, shifter_1_out, shifter_2_out, subtractor_1_out, subtractor_2_out,
       subtractor_3_out, subtractor_4_out, xnor_1_out, xor_1_out;

  Adder #(.width(16)) adder_1 (.a(A), .b(B), .out(adder_1_out), .cout(adder_1_cout));  // open: cin
  Adder #(.width(16)) adder_2 (.a(A), .b(16'h1), .out(adder_2_out), .cout(adder_2_cout));  // open: cin
  Subtractor #(.width(16)) subtractor_1 (
    .a(A), .b(16'h1), .out(subtractor_1_out), .bout(subtractor_1_bout));  // open: bin
  Adder #(.width(16)) adder_3 (.a(A), .b(B), .out(adder_3_out), .cout(adder_3_cout));  // open: cin
  Adder #(.width(16)) adder_4 (.a(adder_1_out), .b(C), .out(adder_4_out), .cin(adder_1_cout), .cout(adder_4_cout));
  Adder #(.width(16)) adder_5 (.a(A), .b(B), .out(adder_5_out), .cin(FlagsInp[0]), .cout(adder_5_cout));
  Subtractor #(.width(16)) subtractor_2 (.a(A), .b(B), .out(subtractor_2_out), .bout(subtractor_2_bout));  // open: bin
  Subtractor #(.width(16)) subtractor_3 (
    .a(A), .b(B), .out(subtractor_3_out), .bin(FlagsInp[0]), .bout(subtractor_3_bout));
  Multiplier multiplier_1 (.a(A[7:0]), .b(B[7:0]), .out(multiplier_1_out), .cout(multiplier_1_cout));  // open: cin
  Subtractor #(.width(16)) subtractor_4 (.a(A), .b(B), .out(subtractor_4_out));  // open: bin, bout
  assign and_1_out = A & B;  // AND_Gate and_1, 16 bits wide
  assign or_1_out = A | B;  // OR_Gate or_1, 16 bits wide
  assign not_1_out = ~A;  // NOT_Gate not_1, 16 bits wide
  Negator #(.width(16)) negator_1 (.in(A), .out(negator_1_out));
  assign xor_1_out = A ^ B;  // XOR_Gate xor_1, 16 bits wide
  assign xnor_1_out = ~(A ^ B);  // XNOR_Gate xnor_1, 16 bits wide
  Shifter #(.width(16)) shifter_1 (.in(A), .\dist (B[3:0]), .out(shifter_1_out));
  Shifter #(.shift("lr"), .width(16)) shifter_2 (.in(A), .\dist (B[3:0]), .out(shifter_2_out));
  Multiplexer #(.select(5), .width(16)) multiplexer_1 (
    .in0(adder_3_out), .in1(adder_4_out), .in2(adder_5_out), .in3(subtractor_2_out), .in4(subtractor_3_out),
    .in5(adder_2_out), .in6(subtractor_1_out), .in7({multiplier_1_cout, multiplier_1_out}),
    .in8(subtractor_4_out), .in9(and_1_out), .in10(or_1_out), .in11(not_1_out), .in12(negator_1_out),
    .in13(xor_1_out), .in14(xnor_1_out), .in15(shifter_1_out), .in16(shifter_2_out), .out(Res), .sel(CMD));  // open: in17, in18, in19, in20, in21, in22, in23, in24, in25, in26, in27, in28, in29, in30, in31
  Multiplexer #(.select(5)) multiplexer_2 (
    .in0(adder_3_cout), .in1(adder_4_cout), .in2(adder_5_cout), .in3(subtractor_2_bout),
    .in4(subtractor_3_bout), .in5(adder_2_cout), .in6(subtractor_1_bout), .in7(1'b0), .in8(1'b0), .in9(1'b0),
    .in10(1'b0), .in11(1'b0), .in12(1'b0), .in13(1'b0), .in14(1'b0), .in15(1'b0), .in16(1'b0),
    .out(Flags[0]), .sel(CMD));  // open: in17, in18, in19, in20, in21, in22, in23, in24, in25, in26, in27, in28, in29, in30, in31
  nor nor_1 (Flags[2], Res[0], Res[1], Res[2], Res[3], Res[4], Res[5], Res[6], Res[7], Res[8], Res[9], Res[10], Res[11], Res[12], Res[13], Res[14], Res[15]);
  not not_2 (Flags[3], Flags[2]);

  assign Flags[1] = 1'b0;

  // Other names for the same wires on the sheet: CarryFlag = Flags[0]; ZeroFlag = Flags[2]

  // Notes on the sheet:
  //   ADD
  //   ADD3
  //   ADC
  //   SUB
  //   SUBC
  //   INC
  //   DEC
  //   MUL
  //   TST
  //   AND
  //   OR
  //   NOT
  //   NEG
  //   XOR
  //   XNOR
  //   SHL
  //   SHR
  //   Flags: 0 - Carry
  //   1 - Overflow
  //   2 - Zero
  //   3 - Not Zero
endmodule

module CU (
  input  [19:0] PMemBus,
  input  CLK,
  input  Reset,
  input  [3:0] Flags,
  output IncPC,
  output out_6,
  output out_7,
  output out_8,
  output [4:0] ALU_CMD,
  output [2:0] A,
  output [2:0] B,
  output [2:0] C,
  output [2:0] Result,
  output Reg_WR_EN,
  output LDC_EN,
  output ALU_EN,
  output MOV_R2R,
  output MOV_R2PC,
  output LDs12C_ALU,
  output Reg_A_EN,
  output PC2ALU_A,
  output Flag_WR_EN,
  output Mem_EN,
  output Mem_WR_EN,
  output out_25,
  output [15:0] LDC,
  output ICI,
  output DBG_cmd
);

  wire comparator_1_eq, DecodeIW, FetchIW, ldc_select_1_ldc_active, multiplexer_1_out, not_1_out, or_1_out;
  wire [1:0] CPU_Status_q;
  wire [2:0] Flag_select, multiplexer_2_out;
  wire [7:0] ldc_select_1_iw_const, multiplexer_4_out, register_1_q;
  wire [7:4] InstructionWord_q;

  Register #(.width(20)) InstructionWord (
    .D(PMemBus), .en(FetchIW), .clk(CLK), .Q({LDC[15:13], C, B, A, InstructionWord_q, LDC[3:0]}), .clr(Reset));
  Counter #(.max('h3), .width(2)) CPU_Status (
    .Q(CPU_Status_q), .clk(CLK), .clr(Reset));  // open: load, D, count, carry, up
  Comparator comparator_1 (.a(8'h5), .b({InstructionWord_q, LDC[3:0]}), .eq(comparator_1_eq));  // open: gt, lt
  Comparator #(.width(20)) comparator_2 (.a(20'h7e), .b(PMemBus), .eq(DBG_cmd));  // open: gt, lt
  not not_1 (not_1_out, comparator_1_eq);
  Multiplexer #(.select(2)) multiplexer_1 (
    .in0(Flags[0]), .in1(Flags[1]), .in2(Flags[2]), .in3(Flags[3]), .out(multiplexer_1_out),
    .sel(Flag_select[1:0]));
  LDC_select ldc_select_1 (
    .IW({InstructionWord_q, LDC[3:0]}), .IW_const(ldc_select_1_iw_const), .LDC_active(ldc_select_1_ldc_active));
  Multiplexer #(.width(3)) multiplexer_2 (
    .in0(LDC[15:13]), .in1(InstructionWord_q[6:4]), .out(multiplexer_2_out), .sel(ldc_select_1_ldc_active));
  or or_1 (or_1_out, multiplexer_1_out, ~Flag_select[2]);  // OR_Gate
  Multiplexer #(.width(3)) multiplexer_3 (.in0(A), .in1(multiplexer_2_out), .out(Result), .sel(not_1_out));
  Multiplexer #(.width(8)) multiplexer_4 (
    .in0(8'h6c), .in1(ldc_select_1_iw_const), .out(multiplexer_4_out), .sel(or_1_out));
  Register register_1 (.D(multiplexer_4_out), .clk(CLK), .Q(register_1_q));  // open: en, clr
  ROM #(.addrWidth(10), .dataWidth(16)) MicroProgramMem (
    .addr({register_1_q, CPU_Status_q}),
    .data({out_25, Mem_WR_EN, Mem_EN, Flag_WR_EN, PC2ALU_A, Reg_A_EN, LDs12C_ALU, MOV_R2PC, MOV_R2R, ALU_EN, LDC_EN, Reg_WR_EN, Flag_select, ICI}));
  and and_1 (DecodeIW, CPU_Status_q[0], ~CPU_Status_q[1]);  // AND_Gate
  and and_2 (FetchIW, ~CPU_Status_q[1], ~CPU_Status_q[0]);  // AND_Gate
  and and_3 (IncPC, CPU_Status_q[0], ~CPU_Status_q[1]);  // AND_Gate
  Multiplexer #(.width(5)) multiplexer_5 (.in0(register_1_q[4:0]), .in1({5{1'b0}}), .out(ALU_CMD), .sel(LDs12C_ALU));

  assign LDC[12:4] = {C, B, A};

  // Notes on the sheet:
  //   Instruction Word
  //   17..19 Result
  //   Carry Overflow Zero notZero
  //   contents of MicroProgramMem (hex, n*v repeats v):
  //   1 1 1441 1451 1 1 1441 1451 1 1 441 1451 1 1 1441 1451 1 1 441 1451 1 1 1441 1451 1 1 1441 1451 1 1
  //   1441 1451 1 1 1441 1441 1 1 1441 1451 1 1 1441 1451 1 1 1441 1451 1 1 1441 1451 1 1 1441 1451 1 1
  //   1441 1451 1 1 1441 1451 1 1 1441 1451 188*0 1 1 81 181 28*0 1 81 81 91 28*0 d 81 81 181 d 8d 8d 18d
  //   f 8f 8f 18f 9 89 89 189 16*0 d a01 a41 b41 d a0d a4d b4d f a0f a4f b4f 9 a09 a49 b49 16*0 4*1 28*0 1
  //   1 4481 4481 1 1 2011 2011 8*0 4*1 68*0 4*1 4*0 1 1 31 31
  //   LSB 4 Bit Inner
  //   MicroProgramMem
  //   useFlags
  //   LDs12C_ALU
  //   Instruction Code implemented
  //   +0010
  //   +0020
  //   +0040
  //   +0080
  //   +0100
  //   +0200
  //   +0400
  //   +0800
  //   +1000
  //   +2000
  //   +4000
  //   Register Write Enable
  //   Load Constant
  //   ALU Enable
  //   Flag Write Enable
  //   Memory Enable
  //   Memory Write Enable
  //   Move Register to Register
  //   Move Register to Program Counter
  //   Load signed 12 bit constant into ALU
  //   CPU Register Port A Enable
  //   Program Counter to ALU A
endmodule

module CPU_Register (
  input  CLK,
  input  [2:0] AddrA,
  input  [2:0] AddrB,
  input  [2:0] AddrC,
  input  Reset,
  input  [15:0] PortIn,
  input  WR_EN,
  input  [2:0] AddrIn,
  output [15:0] PortA,
  output [15:0] PortB,
  output [15:0] PortC
);

  wire decoder_1_out0, decoder_1_out1, decoder_1_out2, decoder_1_out3, decoder_1_out4, decoder_1_out5,
       decoder_1_out6, decoder_1_out7;
  wire [15:0] register_1_q, register_2_q, register_3_q, register_4_q, register_5_q, register_6_q,
       register_7_q, register_8_q;

  Decoder #(.select(3)) decoder_1 (
    .out0(decoder_1_out0), .out1(decoder_1_out1), .out2(decoder_1_out2), .out3(decoder_1_out3),
    .out4(decoder_1_out4), .out5(decoder_1_out5), .out6(decoder_1_out6), .out7(decoder_1_out7), .sel(AddrIn),
    .en(WR_EN));
  Register #(.width(16)) register_1 (.D(PortIn), .en(decoder_1_out0), .clk(CLK), .Q(register_1_q), .clr(Reset));
  Register #(.width(16)) register_2 (.D(PortIn), .en(decoder_1_out1), .clk(CLK), .Q(register_2_q), .clr(Reset));
  Register #(.width(16)) register_3 (.D(PortIn), .en(decoder_1_out2), .clk(CLK), .Q(register_3_q), .clr(Reset));
  Register #(.width(16)) register_4 (.D(PortIn), .en(decoder_1_out3), .clk(CLK), .Q(register_4_q), .clr(Reset));
  Register #(.width(16)) register_5 (.D(PortIn), .en(decoder_1_out4), .clk(CLK), .Q(register_5_q), .clr(Reset));
  Register #(.width(16)) register_6 (.D(PortIn), .en(decoder_1_out5), .clk(CLK), .Q(register_6_q), .clr(Reset));
  Register #(.width(16)) register_7 (.D(PortIn), .en(decoder_1_out6), .clk(CLK), .Q(register_7_q), .clr(Reset));
  Register #(.width(16)) register_8 (.D(PortIn), .en(decoder_1_out7), .clk(CLK), .Q(register_8_q), .clr(Reset));
  Multiplexer #(.select(3), .width(16)) multiplexer_1 (
    .in0(register_1_q), .in1(register_2_q), .in2(register_3_q), .in3(register_4_q), .in4(register_5_q),
    .in5(register_6_q), .in6(register_7_q), .in7(register_8_q), .out(PortA), .sel(AddrA));
  Multiplexer #(.select(3), .width(16)) multiplexer_2 (
    .in0(register_1_q), .in1(register_2_q), .in2(register_3_q), .in3(register_4_q), .in4(register_5_q),
    .in5(register_6_q), .in6(register_7_q), .in7(register_8_q), .out(PortB), .sel(AddrB));
  Multiplexer #(.select(3), .width(16)) multiplexer_3 (
    .in0(register_1_q), .in1(register_2_q), .in2(register_3_q), .in3(register_4_q), .in4(register_5_q),
    .in5(register_6_q), .in6(register_7_q), .in7(register_8_q), .out(PortC), .sel(AddrC));
endmodule

module LDC_select (
  input  [7:0] IW,
  output [7:0] IW_const,
  output LDC_active
);

  wire not_1_out;

  assign IW_const[6:0] = IW[7] ? {7{1'b0}} : 7'bz;  // Controlled_Buffer controlled_buffer_1
  not not_1 (not_1_out, IW[7]);
  assign IW_const[6:0] = not_1_out ? IW[6:0] : 7'bz;  // Controlled_Buffer controlled_buffer_2

  assign IW_const[7] = IW[7];
  assign LDC_active = IW[7];
endmodule
